// Logisim project cifru.circ as structural Verilog
module main (
  input  in_1
);

  wire ADD_out, admin_control_1_admin_reset, clk, comparator_1_egal, comparator_2_egal, comparator_3_egal,
       cu_1_b_led, cu_1_i_led, cu_1_load_1, cu_1_load_2, cu_1_load_3, cu_1_load_4, cu_1_load_5, cu_1_load_6,
       cu_1_reset_counter, cu_1_reset_registrii1, cu_1_reset_registrii2, debouncer_30ns_1_btn_dis,
       debouncer_30ns_2_btn_dis, debouncer_30ns_3_btn_dis, DOWN_out, not_1_out, si_3_1_fout, UP_out;
  wire [3:0] count, mux_1_o, mux_2_o, mux_3_o, r1, r2, r3, r4, r5, r6;
  wire [6:0] hexto7seg_1_seg, hexto7seg_2_seg, hexto7seg_3_seg;

  not not_1 (not_1_out, in_1);
  SI_3 si_3_1 (.i1(comparator_1_egal), .i2(comparator_2_egal), .i3(comparator_3_egal), .fout(si_3_1_fout));
  comparator comparator_1 (.enable(not_1_out), .nr_1(r1), .nr_2(r4), .egal(comparator_1_egal));
  comparator comparator_2 (.enable(not_1_out), .nr_1(r2), .nr_2(r5), .egal(comparator_2_egal));
  comparator comparator_3 (.enable(not_1_out), .nr_1(r3), .nr_2(r6), .egal(comparator_3_egal));
  hexto7seg hexto7seg_1 (.hex_in(mux_1_o), .seg(hexto7seg_1_seg));
  mux mux_1 (.s(cu_1_b_led), .i1(r1), .i2(r4), .o(mux_1_o));
  _7_Segment_Display u_7_segment_display_1 (
    .g(hexto7seg_1_seg[0]), .f(hexto7seg_1_seg[1]), .a(hexto7seg_1_seg[6]), .b(hexto7seg_1_seg[5]),
    .e(hexto7seg_1_seg[2]), .d(hexto7seg_1_seg[3]), .c(hexto7seg_1_seg[4]));  // open: dp
  Button ADD (.out(ADD_out));
  Clock clock_1 (.out(clk));
  Button UP (.out(UP_out));
  Button DOWN (.out(DOWN_out));
  hexto7seg hexto7seg_2 (.hex_in(mux_2_o), .seg(hexto7seg_2_seg));
  mux mux_2 (.s(cu_1_b_led), .i1(r2), .i2(r5), .o(mux_2_o));
  _7_Segment_Display u_7_segment_display_2 (
    .g(hexto7seg_2_seg[0]), .f(hexto7seg_2_seg[1]), .a(hexto7seg_2_seg[6]), .b(hexto7seg_2_seg[5]),
    .e(hexto7seg_2_seg[2]), .d(hexto7seg_2_seg[3]), .c(hexto7seg_2_seg[4]));  // open: dp
  debouncer_30ns debouncer_30ns_1 (.BTN(ADD_out), .CLK_100MHZ(clk), .BTN_DIS(debouncer_30ns_1_btn_dis));
  admin_control admin_control_1 (
    .admin_switch(in_1), .blocat(cu_1_b_led), .reg_4(r4), .reg_5(r5), .reg_6(r6),
    .admin_reset(admin_control_1_admin_reset));
  debouncer_30ns debouncer_30ns_2 (.BTN(UP_out), .CLK_100MHZ(clk), .BTN_DIS(debouncer_30ns_2_btn_dis));
  debouncer_30ns debouncer_30ns_3 (.BTN(DOWN_out), .CLK_100MHZ(clk), .BTN_DIS(debouncer_30ns_3_btn_dis));
  hexto7seg hexto7seg_3 (.hex_in(mux_3_o), .seg(hexto7seg_3_seg));
  mux mux_3 (.s(cu_1_b_led), .i1(r3), .i2(r6), .o(mux_3_o));
  _7_Segment_Display u_7_segment_display_3 (
    .g(hexto7seg_3_seg[0]), .f(hexto7seg_3_seg[1]), .a(hexto7seg_3_seg[6]), .b(hexto7seg_3_seg[5]),
    .e(hexto7seg_3_seg[2]), .d(hexto7seg_3_seg[3]), .c(hexto7seg_3_seg[4]));  // open: dp
  LED INSERT (.in(cu_1_i_led));
  CU cu_1 (
    .ok(debouncer_30ns_1_btn_dis), .reset(admin_control_1_admin_reset), .equal(si_3_1_fout), .clk(clk),
    .i_led(cu_1_i_led), .b_led(cu_1_b_led), .load_1(cu_1_load_1), .load_2(cu_1_load_2), .load_3(cu_1_load_3),
    .load_4(cu_1_load_4), .load_5(cu_1_load_5), .load_6(cu_1_load_6), .reset_counter(cu_1_reset_counter),
    .reset_registrii1(cu_1_reset_registrii1), .reset_registrii2(cu_1_reset_registrii2));
  COUNTER counter_1 (
    .clk(clk), .reset(cu_1_reset_counter), .btn_up(debouncer_30ns_2_btn_dis),
    .btn_down(debouncer_30ns_3_btn_dis), .count(count));
  LED BUSY (.in(cu_1_b_led));
  LED ADMIN (.in(in_1));
  registru registru_1 (.load(cu_1_load_1), .clk(clk), .reset(cu_1_reset_registrii1), .data_in(count), .data_out(r1));
  registru registru_2 (.load(cu_1_load_2), .clk(clk), .reset(cu_1_reset_registrii1), .data_in(count), .data_out(r2));
  registru registru_3 (.load(cu_1_load_3), .clk(clk), .reset(cu_1_reset_registrii1), .data_in(count), .data_out(r3));
  registru registru_4 (.load(cu_1_load_4), .clk(clk), .reset(cu_1_reset_registrii2), .data_in(count), .data_out(r4));
  registru registru_5 (.load(cu_1_load_5), .clk(clk), .reset(cu_1_reset_registrii2), .data_in(count), .data_out(r5));
  registru registru_6 (.load(cu_1_load_6), .clk(clk), .reset(cu_1_reset_registrii2), .data_in(count), .data_out(r6));
endmodule

// VHDL entity registru, as the project stores it:
--REPEDE OANA
LIBRARY ieee;
USE ieee.std_logic_1164.all;

ENTITY registru IS
  PORT ( 
         load, clk, reset: in std_logic;
         data_in:  in std_logic_vector(3 downto 0);
         data_out: out std_logic_vector(3 downto 0)
    );
END registru;


ARCHITECTURE Behavioral OF registru IS
signal sig: std_logic_vector(3 downto 0):="0000";

BEGIN

process (clk, data_in, load)

	begin

		if reset='1' then
			sig<="0000";
		elsif rising_edge(clk)then 
		if load ='1' then
		sig<=data_in;
		end if;
		end if;
	end process;

data_out<=sig;

END Behavioral;

// VHDL entity COUNTER, as the project stores it:
--URECHE SIMONA
LIBRARY ieee;
USE ieee.std_logic_1164.all;
use ieee.std_logic_unsigned.all;

ENTITY COUNTER IS
  PORT (	clk,reset: in std_logic;
  		btn_up, btn_down: in std_logic;
  		
  		count: out std_logic_vector(3 downto 0)
    );
END COUNTER;

ARCHITECTURE Behavioral OF COUNTER IS
    signal value : std_logic_vector(3 downto 0) := "0000";
    signal cont_up, cont_down : std_logic := '0';
    
begin
    process(clk)
    begin
    if reset='1' then
    value<="0000";
    
	
        elsif rising_edge(clk) then
            if btn_up = '1' then
                value <= value + 1;
            end if;
            
            
            if btn_down = '1' then
                value <= value - 1;
            end if;
        end if;
    
	   end process;
count <= value;

END Behavioral;

// VHDL entity comparator, as the project stores it:
--URECHE SIMONA
LIBRARY ieee;
USE ieee.std_logic_1164.all;

ENTITY comparator IS
  PORT ( enable: in std_logic;
         nr_1: in std_logic_vector(3 downto 0);
         nr_2: in std_logic_vector(3 downto 0);
         egal: out std_logic
         
    );
END comparator;

ARCHITECTURE flux OF comparator IS
BEGIN

egal<='1' when nr_1=nr_2 and enable ='1' else '0';

END flux;

// VHDL entity CU, as the project stores it:
--REPEDE OANA+URECHE SIMONA
LIBRARY ieee;
USE ieee.std_logic_1164.all;

ENTITY CU IS
  PORT (ok, reset: in std_logic;
        equal: in std_logic;
        clk: in std_logic;
        i_led, b_led :out std_logic; 
        load_1, load_2, load_3, load_4, load_5, load_6: out std_logic;
        reset_counter: out std_logic; 
        reset_registrii1: out std_logic;
        reset_registrii2: out std_logic
        
             );
END CU;

ARCHITECTURE Behavioral OF CU IS

type stare is (I,P1,D1,T1,L,P2,D2,T2,V);

signal current_state, next_state: stare := I;

BEGIN

process (clk,current_state, next_state) 

begin

if reset='1' then
current_state <= I;

elsif rising_edge(clk) then
current_state <= next_state;
end if;
end process;

process (clk, current_state, next_state) 
begin
case current_state is

when I=>
reset_counter<='1';
reset_registrii1<='1';
reset_registrii2<='1';
b_led<='0';
i_led<='0';
load_1<='0';
load_2<='0';
load_3<='0';
load_4<='0';
load_5<='0';
load_6<='0';


if ok='1' then
i_led<='1';
next_state<=P1;
reset_counter<='1';
else
next_state<=I;
end if;

when P1=>
reset_registrii1<='0';
reset_registrii2<='0';
reset_counter<='0';
load_1<='1';
load_2<='0';
load_3<='0';
load_4<='0';
load_5<='0';
load_6<='0';

if ok='1' then
next_state<=D1;
reset_counter<='1';
else
next_state<=P1;
end if;

when D1=>
reset_counter<='0';
load_1<='0';
load_2<='1';
load_3<='0';
load_4<='0';
load_5<='0';
load_6<='0';
reset_registrii1<='0';
reset_registrii2<='0';
if ok='1' then
reset_counter<='1';
next_state<=T1;
else
next_state<=D1;
end if;

when T1=>
reset_counter<='0';
load_1<='0';
load_2<='0';
load_3<='1';
load_4<='0';
load_5<='0';
load_6<='0';
reset_registrii1<='0';
reset_registrii2<='0';
if ok='1' then
next_state<=L;
else
next_state<=T1;
end if;

when L=>
if ok='1' then
load_1<='0';
load_2<='0';
load_3<='0';
load_4<='0';
load_5<='0';
load_6<='0';
b_led<='1';
i_led<='0';
reset_registrii1<='0';
reset_registrii2<='0';
if ok='1' then
reset_counter<='1';
next_state<=P2;
else
next_state<=L;
end if;
end if;

when P2=>
reset_counter<='0';
load_1<='0';
load_2<='0';
load_3<='0';
load_4<='1';
load_5<='0';
load_6<='0';
reset_registrii1<='0';
reset_registrii2<='0';
if ok='1' then
next_state<=D2;
reset_counter<='1';
else
next_state<=P2;
end if;

when D2=>
reset_counter<='0';
load_1<='0';
load_2<='0';
load_3<='0';
load_4<='0';
load_5<='1';
load_6<='0';
reset_registrii1<='0';
reset_registrii2<='0';
if ok='1' then
reset_counter<='1';
next_state<=T2;
else
next_state<=D2;
end if;

when T2=>
reset_counter<='0';
reset_registrii1<='0';
reset_registrii2<='0';
load_1<='0';
load_2<='0';
load_3<='0';
load_4<='0';
load_5<='0';
load_6<='1';
if ok='1' then
next_state<=V;
else
next_state<=T2;
end if;

when V=>
if equal='0' then
load_1<='0';
load_2<='0';
load_3<='0';
load_4<='0';
load_5<='0';
load_6<='0';
next_state<=L;
reset_registrii2<='1';
else
next_state<=I;
end if;

end case;
end process;
 

END Behavioral;

// VHDL entity mux, as the project stores it:
--REPEDE OANA
LIBRARY ieee;
USE ieee.std_logic_1164.all;

ENTITY mux is
	PORT (
	s:in std_logic;
	i1: in std_logic_vector(3 downto 0);
	i2 :in std_logic_vector(3 downto 0);
	o: out std_logic_vector(3 downto 0)
);
END mux;

ARCHITECTURE flux OF mux IS

BEGIN

o <= i1 when s='0' else i2;

END flux;

// VHDL entity debouncer_30ns, as the project stores it:
--URECHE SIMONA
LIBRARY ieee;
USE ieee.std_logic_1164.all;

ENTITY debouncer_30ns IS
  PORT (
  BTN, CLK_100MHZ: IN STD_LOGIC;
  BTN_DIS: OUT STD_LOGIC
    );
END debouncer_30ns;

ARCHITECTURE structural OF debouncer_30ns IS

COMPONENT bistabil IS
  PORT (
    CLK, D: IN STD_LOGIC;
    Q: OUT STD_LOGIC
    );
END COMPONENT;

SIGNAL Q0: STD_LOGIC := '0';
SIGNAL Q1: STD_LOGIC := '0';
SIGNAL Q2: STD_LOGIC := '0';
BEGIN

D3: bistabil PORT MAP(CLK_100MHZ, Q1, Q2);
D2: bistabil PORT MAP(CLK_100MHZ, Q0, Q1);
D1: bistabil PORT MAP(CLK_100MHZ, BTN, Q0);
BTN_DIS <= (Q0 AND Q1) AND not(Q2);

END structural;


LIBRARY ieee;
USE ieee.std_logic_1164.all;

ENTITY bistabil IS
  PORT (
    CLK, D: IN STD_LOGIC;
    Q: OUT STD_LOGIC
    );
END bistabil;

ARCHITECTURE comportamental OF bistabil IS

BEGIN

PROCESS(CLK)
BEGIN
    IF RISING_EDGE(CLK) THEN
        Q <= D;
    END IF;
END PROCESS;

END comportamental;

// VHDL entity admin_control, as the project stores it:
--REPEDE OANA
LIBRARY ieee;
USE ieee.std_logic_1164.all;

ENTITY admin_control IS
  PORT ( admin_switch: in std_logic;
         blocat: in std_logic;
         admin_reset: out std_logic;
         reg_4, reg_5, reg_6: in std_logic_vector(3 downto 0)
         
    
    );
END admin_control;

ARCHITECTURE flux OF admin_control IS
BEGIN

admin_reset <= '1' when admin_switch='1' and blocat='1' and reg_4="0001" and reg_5="0001"and reg_6="0001" else '0';

END flux;

// VHDL entity hexto7seg, as the project stores it:
--REPEDE OANA 
LIBRARY ieee;
USE ieee.std_logic_1164.all;

ENTITY hexto7seg IS
  PORT (	hex_in: in std_logic_vector(3 downto 0);
		seg: out std_logic_vector( 6 downto 0)
    );
END hexto7seg;

ARCHITECTURE flux OF hexto7seg IS
	begin
		seg <= 	 "1111110" when hex_in = x"0" else
				 "0110000" when hex_in = x"1" else
				 "1101101" when hex_in = x"2" else
				 "1111001" when hex_in = x"3" else
				 "0110011" when hex_in = x"4" else
				 "1011011" when hex_in = x"5" else
				 "1011111" when hex_in = x"6" else
				 "1110000" when hex_in = x"7" else
				 "1111111" when hex_in = x"8" else
				 "1111011" when hex_in = x"9" else
				 "1110111" when hex_in = x"A" else
				 "0011111" when hex_in = x"B" else
				 "1001110" when hex_in = x"C" else
				 "0111101" when hex_in = x"D" else
				 "1001111" when hex_in = x"E" else
				 "1000111" when hex_in = x"F" else
				 "0000000";
END flux;

// VHDL entity SI_3, as the project stores it:
--URECHE SIMONA
LIBRARY ieee;
USE ieee.std_logic_1164.all;

ENTITY SI_3 IS
  PORT (
		i1,i2,i3: in std_logic;
		fout: out std_logic
    );
END SI_3;


ARCHITECTURE TypeArchitecture OF SI_3 IS
BEGIN
	fout <= i1 and i2 and i3;

END TypeArchitecture;
